// Logisim project trabalho.circ as structural Verilog: 1 circuit, main circuit main
module main (
  input  in_1,
  input  in_2,
  input  in_3,
  input  in_4,
  input  in_5,
  input  in_6,
  input  in_7,
  input  in_8,
  input  in_9,
  input  in_10,
  input  in_11,
  input  in_12,
  input  in_13,
  input  in_14,
  input  in_15,
  input  in_16,
  input  in_17,
  input  in_18,
  input  in_19,
  input  in_20,
  input  in_21,
  input  in_22,
  input  in_23,
  input  in_24
);

  _7_Segment_Display u_7_segment_display_1 (
    .g(in_1), .f(in_1), .a(in_1), .b(in_1), .e(in_13), .d(in_13), .c(in_13));  // open: dp
  _7_Segment_Display u_7_segment_display_2 (
    .g(in_3), .f(in_3), .a(in_3), .b(in_3), .e(in_16), .c(in_16));  // open: d, dp
  _7_Segment_Display u_7_segment_display_3 (.f(in_6), .b(in_6), .e(in_18), .d(in_18), .c(in_18));  // open: g, a, dp
  _7_Segment_Display u_7_segment_display_4 (.g(in_10), .e(in_22), .c(in_22));  // open: f, a, b, d, dp
  _7_Segment_Display u_7_segment_display_5 (
    .f(in_12), .a(in_12), .b(in_12), .e(in_24), .d(in_24), .c(in_24));  // open: g, dp
endmodule
